# Fritzing sketch P2fritzing (saved by Fritzing 0.9.3b)
breadboards: 1

parts:
  Part1 = Bluetooth HC-05 Macho  # not connected
  Part2 = Arduino Uno (Rev3)
  T1 = LM35 Temperature Sensor [package="TO92 [THT]"]
  R1 = Photocell (LDR) [package=THT]
  hc-sr2 = hc-sr04
  LED2 = LED - 5mm [color="Red (633nm)" package="5 mm [THT]"]
  J1 = Piezo Speaker
  R2 = Resistor [tolerance=±5% resistance=220 package=THT]
  R3 = Resistor [tolerance=±5% resistance=220 package=THT]

nets:
  N1: Part2.A0, R1.pin_1
  N2: Part2.A1, LED2.anode
  N3: Part2.A2, T1.Vout
  N4: Part2.D11_PWM/MOSI, hc-sr2.Echo
  N5: Part2.D12/MISO, hc-sr2.Trig
  N6: Part2.D13/SCK, J1.pin2
  GND: Part2.GND, T1.GND, hc-sr2.GND, J1.pin1, R2.Pin_1, R3.Pin_0
  5V: Part2.5V, T1.+Vs, R1.pin_0, hc-sr2.VCC, R2.Pin_0
  N7: LED2.cathode, R3.Pin_1
